// Logisim project 32-bit Adder Circuit [Jubayer Alam].circ as structural Verilog: 5 circuits, main circuit main
module main (
  input  [31:0] A,
  input  [31:0] B,
  input  Cin,
  output [31:0] Sum,
  output Cout
);

  wire n16_bit_adder_circuit_1_cout;

  _16_bit_Adder_Circuit u_16_bit_adder_circuit_1 (
    .A(A[15:0]), .B(B[15:0]), .Cin(Cin), .Cout(n16_bit_adder_circuit_1_cout), .S(Sum[15:0]));
  _16_bit_Adder_Circuit u_16_bit_adder_circuit_2 (
    .A(A[31:16]), .B(B[31:16]), .Cin(n16_bit_adder_circuit_1_cout), .Cout(Cout), .S(Sum[31:16]));

  // Notes on the sheet:
  //   32 Bit Adder Circuit
  //   Name: Jubayer Alam
  //   ID: 1420268042
  //   16 Bit Adder
  //   16 Bit Adder
endmodule

module Full_Adder_Circuit (
  input  Cin,
  input  A,
  input  B,
  output S,
  output Cout
);

  wire AND_2_out, AND_out, XOR_out;

  xor XOR (XOR_out, A, B);
  xor XOR_2 (S, XOR_out, Cin);
  and AND (AND_out, Cin, XOR_out);
  and AND_2 (AND_2_out, B, A);
  or OR (Cout, AND_out, AND_2_out);

  // Notes on the sheet:
  //   Full Adder Circuit
endmodule

// 4 bit adder
module _4_bit_Adder_Circuit (
  input  Cin,
  input  A1,
  input  A2,
  input  A3,
  input  A4,
  input  B1,
  input  B2,
  input  B3,
  input  B4,
  output S1,
  output S2,
  output S3,
  output S4,
  output Cout
);

  wire FA1_cout, FA2_cout, FA3_cout;

  Full_Adder_Circuit FA1 (.A(A1), .B(B1), .S(S1), .Cin(Cin), .Cout(FA1_cout));
  Full_Adder_Circuit FA2 (.A(A2), .B(B2), .S(S2), .Cin(FA1_cout), .Cout(FA2_cout));
  Full_Adder_Circuit FA3 (.A(A3), .B(B3), .S(S3), .Cin(FA2_cout), .Cout(FA3_cout));
  Full_Adder_Circuit FA4 (.A(A4), .B(B4), .S(S4), .Cin(FA3_cout), .Cout(Cout));

  // Notes on the sheet:
  //   4 Bit Adder Circuit
endmodule

// 8 bit adder
module _8_bit_Adder_Circuit (
  input  Cin,
  input  A1,
  input  A2,
  input  A3,
  input  A4,
  input  A5,
  input  A6,
  input  A7,
  input  A8,
  input  B1,
  input  B2,
  input  B3,
  input  B4,
  input  B5,
  input  B6,
  input  B7,
  input  B8,
  output S1,
  output S2,
  output S3,
  output S4,
  output S5,
  output S6,
  output S7,
  output S8,
  output Cout
);

  wire n4_bit_adder_circuit_1_cout;

  _4_bit_Adder_Circuit u_4_bit_adder_circuit_1 (
    .A1(A1), .A2(A2), .A3(A3), .A4(A4), .B1(B1), .B2(B2), .B3(B3), .B4(B4), .Cin(Cin),
    .Cout(n4_bit_adder_circuit_1_cout), .S1(S1), .S2(S2), .S3(S3), .S4(S4));
  _4_bit_Adder_Circuit u_4_bit_adder_circuit_2 (
    .A1(A5), .A2(A6), .A3(A7), .A4(A8), .B1(B5), .B2(B6), .B3(B7), .B4(B8),
    .Cin(n4_bit_adder_circuit_1_cout), .Cout(Cout), .S1(S5), .S2(S6), .S3(S7), .S4(S8));

  // Notes on the sheet:
  //   8 Bit Adder Circuit
endmodule

module _16_bit_Adder_Circuit (
  input  Cin,
  input  [15:0] A,
  input  [15:0] B,
  output [15:0] S,
  output Cout
);

  wire n8_bit_adder_circuit_1_cout;

  _8_bit_Adder_Circuit u_8_bit_adder_circuit_1 (
    .A1(A[0]), .A2(A[1]), .A3(A[2]), .A4(A[3]), .A5(A[4]), .A6(A[5]), .A7(A[6]), .A8(A[7]), .B1(B[0]),
    .B2(B[1]), .B3(B[2]), .B4(B[3]), .B5(B[4]), .B6(B[5]), .B7(B[6]), .B8(B[7]), .Cin(Cin),
    .Cout(n8_bit_adder_circuit_1_cout), .S1(S[0]), .S2(S[1]), .S3(S[2]), .S4(S[3]), .S5(S[4]), .S6(S[5]),
    .S7(S[6]), .S8(S[7]));
  _8_bit_Adder_Circuit u_8_bit_adder_circuit_2 (
    .A1(A[8]), .A2(A[9]), .A3(A[10]), .A4(A[11]), .A5(A[12]), .A6(A[13]), .A7(A[14]), .A8(A[15]), .B1(B[8]),
    .B2(B[9]), .B3(B[10]), .B4(B[11]), .B5(B[12]), .B6(B[13]), .B7(B[14]), .B8(B[15]),
    .Cin(n8_bit_adder_circuit_1_cout), .Cout(Cout), .S1(S[8]), .S2(S[9]), .S3(S[10]), .S4(S[11]), .S5(S[12]),
    .S6(S[13]), .S7(S[14]), .S8(S[15]));

  // Notes on the sheet:
  //   16 Bit Adder Circuit
endmodule
